# Fritzing sketch Projet_ELEC (saved by Fritzing 0.9.6b)

parts:
  LCD1 = LCD screen
  Mod1 = Raspberry Pi 4B
  HC-SR04_Sensor_1 = HC-SR04 Ultrasonic Distance Sensor
  M2 = DC Motor
  Grove1 = Grove Light Sensor
  Grove2 = Grove Light Sensor
  Grove3 = Grove Light Sensor
  LCM1602_IIC1 = LCM1602 IIC [part_number="LCM1602 IIC" chip_label="LCM1602 IIC" package="DIP (Dual Inline) [THT]"]
  M1 = DC Motor
  Mod2 = Passive Buzzer
  VCC1 = 4 x AAA Battery Mount
  IC1 = L293D [package=THT]

nets:
  VSS: LCD1.VSS, LCM1602_IIC1.VSS
  VDD: LCD1.VDD, LCM1602_IIC1.VDD
  N1: LCD1.V0, LCM1602_IIC1.V0
  N2: LCD1.RS, LCM1602_IIC1.RS
  N3: LCD1.R/W, LCM1602_IIC1.RW
  N4: LCD1.E, LCM1602_IIC1.E
  N5: LCD1.DB0, LCM1602_IIC1.D0
  N6: LCD1.DB1, LCM1602_IIC1.D1
  N7: LCD1.DB2, LCM1602_IIC1.D2
  N8: LCD1.DB3, LCM1602_IIC1.D3
  N9: LCD1.DB4, LCM1602_IIC1.D4
  N10: LCD1.DB5, LCM1602_IIC1.D5
  N11: LCD1.DB6, LCM1602_IIC1.D6
  N12: LCD1.DB7, LCM1602_IIC1.D7
  N13: LCD1.LED+, LCM1602_IIC1.A
  N14: LCD1.LED-, LCM1602_IIC1.K
  VCC: Mod1.3V3, HC-SR04_Sensor_1.VCC, Grove1.VCC, Grove2.VCC, Grove3.VCC
  5V: Mod1.5V, LCM1602_IIC1.VCC, IC1.+V
  N15: Mod1.GPIO2, LCM1602_IIC1.SDA
  N16: Mod1.GPIO3, LCM1602_IIC1.SCL
  GND: Mod1.GND, HC-SR04_Sensor_1.GND, Grove1.GND, Grove2.GND, Grove3.GND, LCM1602_IIC1.GND, Mod2.-, VCC1.-, IC1.0V
  N17: Mod1.GPIO14, Mod2.NC
  N18: Mod1.GPIO17, Grove3.SIG
  N19: Mod1.GPIO27, Grove1.SIG
  N20: Mod1.GPIO22, Grove2.SIG
  N21: Mod1.GPIO25, HC-SR04_Sensor_1.TRIG
  N22: Mod1.GPIO8, HC-SR04_Sensor_1.ECHO
  N23: Mod1.GPIO5, IC1.In_1
  N24: Mod1.GPIO6, IC1.In_2
  N25: Mod1.GPIO12, IC1.Enable_2
  N26: Mod1.GPIO13, IC1.Enable_1
  N27: Mod1.GPIO26, IC1.In_3
  N28: Mod1.GPIO21, IC1.In_4
  N29: M2.pin_1, IC1.Out_4_(_Controlled_by_Enable_2_)
  N30: M2.pin_2, IC1.Out_3_(_Controlled_by_Enable_2_)
  N31: M1.pin_1, IC1.Out_2_(_Controlled_by_Enable_1_)
  N32: M1.pin_2, IC1.Out_1_(_Controlled_by_Enable_1_)
  N33: VCC1.+, IC1.+Vmotor

custom parts:
  LCM1602 IIC: I2C-Module to use a 1602 or 2004 LCD on with the wire.h libory Serial LCD Modul
